// Logisim project s-mips.circ as structural Verilog: 6 circuits, main circuit S-MIPS Board
module S_MIPS_Board (
  input  DESHABILITAR_DISPATCHER,
  output halt
);

  wire button_1_out, CLK, CS, d_ff_1_q, LCLR, LoadRAM, LoadRAMOn, LW, R_R_W, R_W, ram_dispatcher_1_finished,
       RCS, Reset_out, RST, TTY_EN;
  wire [2:0] KDB;
  wire [3:0] LMask, Mask, ram_1_read_time, ram_1_write_time, RMask;
  wire [6:0] KDB_DATA, TTY_DATA;
  wire [15:0] Addr, LAddr, RAddr;
  wire [31:0] I0, I1, I2, I3, LData, ram_1_data_out_0, ram_1_data_out_1, ram_1_data_out_2, ram_1_data_out_3,
       RI0, RI1, RI2, RI3;

  TTY #(.rows(25), .cols(80)) tty_1 (.data(TTY_DATA), .clk(CLK), .we(TTY_EN), .clr(RST));
  not not_1 (LoadRAMOn, ram_dispatcher_1_finished);
  RAM_Dispatcher ram_dispatcher_1 (
    .WriteTime(ram_1_write_time), .Clock(CLK), .Data(LData), .Address(LAddr), .Mask(LMask),
    .Finished(ram_dispatcher_1_finished), .Write(LW), .CLR(LCLR));
  Keyboard #(.buflen(64)) keyboard_1 (.clk(CLK), .re(KDB[0]), .avail(KDB[2]), .data(KDB_DATA));  // open: clr
  RAM ram_1 (
    .Address(RAddr), .Data_Out_0(ram_1_data_out_0), .Data_Out_1(ram_1_data_out_1),
    .Data_Out_2(ram_1_data_out_2), .Data_Out_3(ram_1_data_out_3), .Data_In_0(RI0), .Data_In_1(RI1),
    .Data_In_2(RI2), .Data_In_3(RI3), .Mask(RMask), .nRead_Write(R_R_W), .Chip_Select(RCS),
    .Read_Time(ram_1_read_time), .Reset(button_1_out), .Write_Time(ram_1_write_time));
  Button button_1 (.out(button_1_out));
  D_Flip_Flop d_ff_1 (.clk(CLK), .D(1'b1), .Q(d_ff_1_q), .reset(Reset_out));  // open: Qn, preset, en
  Button Reset (.out(Reset_out));
  S_MIPS s_mips_1 (
    .Kbd_Enable(KDB[0]), .Address(Addr), .Kbd_Clear(KDB[1]), .Kbd_Available(KDB[2]), .RAM_In_0(I0),
    .Kbd_ASCII_Data(KDB_DATA), .RAM_In_1(I1), .TTY_Enable(TTY_EN), .RAM_In_2(I2), .RAM_In_3(I3),
    .TTY_ASCII_Data(TTY_DATA), .Reset(RST), .RAM_Out_0(ram_1_data_out_0), .Clock(CLK),
    .RAM_Out_1(ram_1_data_out_1), .Stop(halt), .RAM_Out_2(ram_1_data_out_2), .RAM_Out_3(ram_1_data_out_3),
    .Mask(Mask), .Read_Time(ram_1_read_time), .Write_Time(ram_1_write_time), .nRead_Write(R_W),
    .Chip_Select(CS));
  D_Flip_Flop d_ff_2 (.clk(CLK), .D(d_ff_1_q), .Qn(LCLR), .reset(Reset_out));  // open: Q, preset, en
  or or_1 (RST, LCLR, LoadRAM);
  Clock clock_1 (.out(CLK));
  Multiplexer #(.width(32), .enable("false")) multiplexer_1 (.in0(I0), .in1(LData), .out(RI0), .sel(LoadRAM));
  Multiplexer #(.width(32), .enable("false")) multiplexer_2 (.in0(I1), .in1(LData), .out(RI1), .sel(LoadRAM));
  Multiplexer #(.width(32), .enable("false")) multiplexer_3 (.in0(I2), .in1(LData), .out(RI2), .sel(LoadRAM));
  Multiplexer #(.width(32), .enable("false")) multiplexer_4 (.in0(I3), .in1(LData), .out(RI3), .sel(LoadRAM));
  and and_1 (LoadRAM, ~DESHABILITAR_DISPATCHER, LoadRAMOn);  // AND_Gate
  Multiplexer #(.width(16), .enable("false")) multiplexer_5 (.in0(Addr), .in1(LAddr), .out(RAddr), .sel(LoadRAM));
  Multiplexer #(.width(4), .enable("false")) multiplexer_6 (.in0(Mask), .in1(LMask), .out(RMask), .sel(LoadRAM));
  Multiplexer #(.enable("false")) multiplexer_7 (.in0(CS), .in1(LW), .out(RCS), .sel(LoadRAM));
  Multiplexer #(.enable("false")) multiplexer_8 (.in0(R_W), .in1(LW), .out(R_R_W), .sel(LoadRAM));

  // Notes on the sheet:
  //   NO MODIFICAR
  //   Keyboard
endmodule

module RAM (
  input  [15:0] Address,
  input  [31:0] Data_In_0,
  input  [31:0] Data_In_1,
  input  [31:0] Data_In_2,
  input  [31:0] Data_In_3,
  input  [3:0] Mask,
  input  nRead_Write,
  input  Chip_Select,
  input  Reset,
  output [31:0] Data_Out_0,
  output [31:0] Data_Out_1,
  output [31:0] Data_Out_2,
  output [31:0] Data_Out_3,
  output [3:0] Read_Time,
  output [3:0] Write_Time
);

  wire and_2_out, and_3_out, and_4_out, and_5_out, and_6_out, and_7_out, and_8_out, and_9_out, Changed, CLK,
       comparator_2_eq, comparator_3_eq, comparator_4_eq, comparator_5_eq, comparator_6_eq, Count,
       demultiplexer_3_out0, Idle, Idle_q, Load, Load0, Load1, nand_1_out, or_1_out, or_2_out, or_3_out,
       or_4_out, or_5_out, or_6_out, or_7_out, or_8_out, or_9_out, or_10_out, Proc_q, Update_Mem, Zero_Time;
  wire [3:0] counter_1_q, multiplexer_1_out, subtractor_1_out;
  wire [31:0] register_1_q, register_2_q, register_3_q, register_4_q, register_5_q;

  // Probe on 4'b0011
  // Probe on 4'b0010
  Multiplexer #(.width(4), .enable("false")) multiplexer_1 (
    .in0(4'b0011), .in1(4'b0010), .out(multiplexer_1_out), .sel(nRead_Write));
  or or_1 (or_1_out, Idle, Update_Mem);
  or or_2 (or_2_out, ~Chip_Select, Reset);  // OR_Gate
  Subtractor #(.width(4)) subtractor_1 (.a(multiplexer_1_out), .b(4'b0010), .out(subtractor_1_out));  // open: bin, bout
  Demultiplexer #(.enable("false")) demultiplexer_1 (.out0(Idle), .out1(Load0), .in(Idle_q), .sel(Changed));
  D_Flip_Flop u_Idle (.clk(CLK), .D(or_1_out), .Q(Idle_q), .preset(or_2_out));  // open: Qn, en, reset
  // Probe on counter_1_q
  Counter #(.width(4), .max('hf)) counter_1 (
    .load(Load), .D(subtractor_1_out), .count(Count), .Q(counter_1_q), .clk(CLK), .clr(or_3_out));  // open: carry
  or or_3 (or_3_out, ~Chip_Select, Reset);  // OR_Gate
  Comparator #(.width(4), .mode("unsigned")) comparator_1 (
    .a(4'b0000), .b(counter_1_q), .eq(Zero_Time));  // open: gt, lt
  or or_4 (or_4_out, Count, Load0, Load1);
  Register #(.width(32)) register_1 (.D(Data_In_0), .en(Chip_Select), .Q(register_1_q), .clk(CLK), .clr(or_5_out));
  or or_5 (or_5_out, ~Chip_Select, Reset);  // OR_Gate
  Register #(.width(32)) register_2 (.D(Data_In_1), .en(Chip_Select), .Q(register_2_q), .clk(CLK), .clr(or_6_out));
  or or_6 (or_6_out, ~Chip_Select, Reset);  // OR_Gate
  Register #(.width(32)) register_3 (.D(Data_In_2), .en(Chip_Select), .Q(register_3_q), .clk(CLK), .clr(or_7_out));
  or or_7 (or_7_out, ~Chip_Select, Reset);  // OR_Gate
  Register #(.width(32)) register_4 (.D(Data_In_3), .en(Chip_Select), .Q(register_4_q), .clk(CLK), .clr(or_8_out));
  or or_8 (or_8_out, ~Chip_Select, Reset);  // OR_Gate
  Register #(.width(32)) register_5 (
    .D({{11{1'b1}}, nRead_Write, Mask, Address}), .en(Chip_Select), .Q(register_5_q), .clk(CLK),
    .clr(or_9_out));
  or or_9 (or_9_out, ~Chip_Select, Reset);  // OR_Gate
  D_Flip_Flop Proc (.clk(CLK), .D(or_4_out), .Q(Proc_q), .reset(or_10_out));  // open: Qn, preset, en
  or or_10 (or_10_out, ~Chip_Select, Reset);  // OR_Gate
  Demultiplexer #(.enable("false")) demultiplexer_2 (
    .out0(Count), .out1(Update_Mem), .in(demultiplexer_3_out0), .sel(Zero_Time));
  Demultiplexer #(.enable("false")) demultiplexer_3 (
    .out0(demultiplexer_3_out0), .out1(Load1), .in(Proc_q), .sel(Changed));
  Clock clock_1 (.out(CLK));
  Comparator #(.width(32)) comparator_2 (.a(register_1_q), .b(Data_In_0), .eq(comparator_2_eq));  // open: gt, lt
  Comparator #(.width(32)) comparator_3 (.a(register_2_q), .b(Data_In_1), .eq(comparator_3_eq));  // open: gt, lt
  Comparator #(.width(32)) comparator_4 (.a(register_3_q), .b(Data_In_2), .eq(comparator_4_eq));  // open: gt, lt
  Comparator #(.width(32)) comparator_5 (.a(register_4_q), .b(Data_In_3), .eq(comparator_5_eq));  // open: gt, lt
  Comparator #(.width(32)) comparator_6 (
    .a(register_5_q), .b({{11{1'b1}}, nRead_Write, Mask, Address}), .eq(comparator_6_eq));  // open: gt, lt
  nand nand_1 (nand_1_out, comparator_6_eq, comparator_2_eq, comparator_3_eq, comparator_4_eq, comparator_5_eq);
  and and_1 (Changed, nand_1_out, Chip_Select);
  or or_11 (Load, Count, Load1, Load0);
  and and_2 (and_2_out, Mask[0], Update_Mem, nRead_Write);
  and and_3 (and_3_out, Mask[1], Update_Mem, nRead_Write);
  and and_4 (and_4_out, Mask[2], Update_Mem, nRead_Write);
  and and_5 (and_5_out, Mask[3], Update_Mem, nRead_Write);
  RAM_part #(.addrWidth(16), .dataWidth(32), .bus("separate")) ram_1 (
    .addr(Address), .din(Data_In_0), .data(Data_Out_0), .str(and_2_out), .sel(Chip_Select), .clk(CLK),
    .ld(and_6_out), .clr(Reset));
  and and_6 (and_6_out, ~nRead_Write, Idle);  // AND_Gate
  RAM_part #(.addrWidth(16), .dataWidth(32), .bus("separate")) ram_2 (
    .addr(Address), .din(Data_In_1), .data(Data_Out_1), .str(and_3_out), .sel(Chip_Select), .clk(CLK),
    .ld(and_7_out), .clr(Reset));
  and and_7 (and_7_out, ~nRead_Write, Idle);  // AND_Gate
  RAM_part #(.addrWidth(16), .dataWidth(32), .bus("separate")) ram_3 (
    .addr(Address), .din(Data_In_2), .data(Data_Out_2), .str(and_4_out), .sel(Chip_Select), .clk(CLK),
    .ld(and_8_out), .clr(Reset));
  and and_8 (and_8_out, ~nRead_Write, Idle);  // AND_Gate
  RAM_part #(.addrWidth(16), .dataWidth(32), .bus("separate")) ram_4 (
    .addr(Address), .din(Data_In_3), .data(Data_Out_3), .str(and_5_out), .sel(Chip_Select), .clk(CLK),
    .ld(and_9_out), .clr(Reset));
  and and_9 (and_9_out, ~nRead_Write, Idle);  // AND_Gate

  assign Read_Time = 4'b0011;
  assign Write_Time = 4'b0010;

  // Other names for the same wires on the sheet: M0 = Mask[0]; M1 = Mask[1]; M2 = Mask[2]; M3 = Mask[3];
  //   RW = nRead_Write; CLR = Reset; CS = Chip_Select; Load2 = Count

  // Notes on the sheet:
  //   NO MODIFICAR
  //   excepto quizás los valores RT y WT
  //   BANK0
  //   BANK1
  //   BANK2
  //   BANK3
endmodule

module S_MIPS (
  input  Kbd_Available,
  input  [6:0] Kbd_ASCII_Data,
  input  [31:0] RAM_Out_0,
  input  [31:0] RAM_Out_1,
  input  Reset,
  input  [31:0] RAM_Out_2,
  input  Clock,
  input  [31:0] RAM_Out_3,
  input  [3:0] Read_Time,
  input  [3:0] Write_Time,
  output Kbd_Enable,
  output [15:0] Address,
  output Kbd_Clear,
  output TTY_Enable,
  output [6:0] TTY_ASCII_Data,
  output Stop,
  output [31:0] RAM_In_0,
  output [31:0] RAM_In_1,
  output [31:0] RAM_In_2,
  output [31:0] RAM_In_3,
  output [3:0] Mask,
  output nRead_Write,
  output Chip_Select
);


  // Other names for the same wires on the sheet: CLK = Clock; CLR = Reset; CS = Chip_Select;
  //   KBD_AVAIL = Kbd_Available; KBD_CLR = Kbd_Clear; KBD_DATA[6:0] = Kbd_ASCII_Data; RAM_A[15:0] = Address;
  //   RAM_INPUT_0[31:0] = RAM_In_0; RAM_INPUT_1[31:0] = RAM_In_1; RAM_INPUT_2[31:0] = RAM_In_2;
  //   RAM_INPUT_3[31:0] = RAM_In_3; RAM_MASK[3:0] = Mask; RAM_OUTPUT_0[31:0] = RAM_Out_0;
  //   RAM_OUTPUT_1[31:0] = RAM_Out_1; RAM_OUTPUT_2[31:0] = RAM_Out_2; RAM_OUTPUT_3[31:0] = RAM_Out_3;
  //   RW = nRead_Write; TTY_DATA[6:0] = TTY_ASCII_Data

  // Notes on the sheet:
  //   RAM ADDRESS
  //   DATA FROM RAM
  //   DATA TO RAM
  //   DATA WRITE MASK
  //   RAM TIMING
  //   RAM CONTROL
  //   KEYBOARD
  //   TTY
  //   SEQUENCING
endmodule

module RAM_Dispatcher (
  input  [3:0] WriteTime,
  input  Clock,
  input  CLR,
  output [31:0] Data,
  output [15:0] Address,
  output [3:0] Mask,
  output Finished,
  output Write
);

  wire demultiplexer_2_out1, demultiplexer_3_out1, End, IDLE_q, IncAddr, Load, or_1_out, or_2_out, While_q,
       WriteEnd;
  wire [3:0] counter_1_q;
  wire [31:0] CurrentAddress_q;

  Counter #(.width(32), .max('hffffffff)) CurrentAddress (
    .count(IncAddr), .Q({CurrentAddress_q[31:18], Address, CurrentAddress_q[1:0]}), .clk(Clock), .clr(CLR));  // open: load, D, carry
  or or_1 (or_1_out, IncAddr, demultiplexer_3_out1, Finished);
  D_Flip_Flop IDLE (.clk(Clock), .D(or_1_out), .Q(IDLE_q), .preset(CLR));  // open: Qn, en, reset
  Demultiplexer #(.enable("false")) demultiplexer_1 (.out0(Load), .out1(Finished), .in(IDLE_q), .sel(End));
  D_Flip_Flop While (.clk(Clock), .D(or_2_out), .Q(While_q), .reset(CLR));  // open: Qn, preset, en
  or or_2 (or_2_out, Write, Load);
  RAM_part #(.addrWidth(18), .dataWidth(32)) ram_1 (
    .addr({Address, CurrentAddress_q[1:0]}), .data(Data), .clk(Clock));  // open: sel, ld, clr
  Demultiplexer #(.enable("false")) demultiplexer_2 (
    .out0(Write), .out1(demultiplexer_2_out1), .in(While_q), .sel(WriteEnd));
  Decoder #(.select(2)) decoder_1 (
    .out0(Mask[0]), .out1(Mask[1]), .out2(Mask[2]), .out3(Mask[3]), .sel(CurrentAddress_q[1:0]));  // open: en
  Demultiplexer #(.enable("false")) demultiplexer_3 (
    .out0(IncAddr), .out1(demultiplexer_3_out1), .in(demultiplexer_2_out1), .sel(End));
  Counter #(.width(4), .max('hf)) counter_1 (
    .load(Load), .D(WriteTime), .count(Write), .Q(counter_1_q), .clk(Clock));  // open: carry, clr
  Comparator #(.width(32)) comparator_1 (.a(Data), .b({32{1'b1}}), .eq(End));  // open: gt, lt
  Comparator #(.width(4)) comparator_2 (.a(4'b0000), .b(counter_1_q), .eq(WriteEnd));  // open: gt, lt

  // Other names for the same wires on the sheet: CLK = Clock; Count = Write; WT[3:0] = WriteTime
endmodule

module RegisterFile (
  input  [4:0] Data_Address,
  input  [31:0] in_2,
  input  Read_Write,
  input  [4:0] Selector_A,
  input  [4:0] Selector_B,
  input  Clock,
  input  Reset,
  output [31:0] Output,
  output [31:0] Output_2
);

  wire E00, E01, E02, E03, E04, E05, E06, E07, E08, E09, E10, E11, E12, E13, E14, E15, E16, E17, E18, E19,
       E20, E21, E22, E23, E24, E25, E26, E27, E28, E29, E30, E31;
  wire [31:0] Ou07, Out00, Out01, Out02, Out03, Out04, Out05, Out06, Out07, Out08, Out09, Out10, Out11,
       Out12, Out13, Out14, Out15, Out16, Out17, Out18, Out19, Out20, Out21, Out22, Out23, Out24, Out25,
       Out26, Out27, Out28, Out29, Out30, Out31;

  Demultiplexer #(.select(5), .enable("false")) demultiplexer_1 (
    .out0(E00), .out1(E01), .out2(E02), .out3(E03), .out4(E04), .out5(E05), .out6(E06), .out7(E07),
    .out8(E08), .out9(E09), .out10(E10), .out11(E11), .out12(E12), .out13(E13), .out14(E14), .out15(E15),
    .out16(E16), .out17(E17), .out18(E18), .out19(E19), .out20(E20), .out21(E21), .out22(E22), .out23(E23),
    .out24(E24), .out25(E25), .out26(E26), .out27(E27), .out28(E28), .out29(E29), .out30(E30), .out31(E31),
    .in(Read_Write), .sel(Data_Address));
  Register #(.width(32)) R00 (.D({32{1'b0}}), .en(E00), .Q(Out00), .clk(Clock), .clr(Reset));
  Register #(.width(32)) R04 (.D(in_2), .en(E04), .Q(Out04), .clk(Clock), .clr(Reset));
  Register #(.width(32)) R08 (.D(in_2), .en(E08), .Q(Out08), .clk(Clock), .clr(Reset));
  Register #(.width(32)) R12 (.D(in_2), .en(E12), .Q(Out12), .clk(Clock), .clr(Reset));
  Register #(.width(32)) R16 (.D(in_2), .en(E16), .Q(Out16), .clk(Clock), .clr(Reset));
  Register #(.width(32)) R20 (.D(in_2), .en(E20), .Q(Out20), .clk(Clock), .clr(Reset));
  Register #(.width(32)) R24 (.D(in_2), .en(E24), .Q(Out24), .clk(Clock), .clr(Reset));
  Register #(.width(32)) R28 (.D(in_2), .en(E28), .Q(Out28), .clk(Clock), .clr(Reset));
  Register #(.width(32)) R01 (.D(in_2), .en(E01), .Q(Out01), .clk(Clock), .clr(Reset));
  Register #(.width(32)) R05 (.D(in_2), .en(E05), .Q(Out05), .clk(Clock), .clr(Reset));
  Register #(.width(32)) R09 (.D(in_2), .en(E09), .Q(Out09), .clk(Clock), .clr(Reset));
  Register #(.width(32)) R13 (.D(in_2), .en(E13), .Q(Out13), .clk(Clock), .clr(Reset));
  Register #(.width(32)) R17 (.D(in_2), .en(E17), .Q(Out17), .clk(Clock), .clr(Reset));
  Register #(.width(32)) R21 (.D(in_2), .en(E21), .Q(Out21), .clk(Clock), .clr(Reset));
  Register #(.width(32)) R25 (.D(in_2), .en(E25), .Q(Out25), .clk(Clock), .clr(Reset));
  Register #(.width(32)) R29 (.D(in_2), .en(E29), .Q(Out29), .clk(Clock), .clr(Reset));
  Register #(.width(32)) R02 (.D(in_2), .en(E02), .Q(Out02), .clk(Clock), .clr(Reset));
  Register #(.width(32)) R06 (.D(in_2), .en(E06), .Q(Out06), .clk(Clock), .clr(Reset));
  Register #(.width(32)) R10 (.D(in_2), .en(E10), .Q(Out10), .clk(Clock), .clr(Reset));
  Register #(.width(32)) R14 (.D(in_2), .en(E14), .Q(Out14), .clk(Clock), .clr(Reset));
  Register #(.width(32)) R18 (.D(in_2), .en(E18), .Q(Out18), .clk(Clock), .clr(Reset));
  Register #(.width(32)) R22 (.D(in_2), .en(E22), .Q(Out22), .clk(Clock), .clr(Reset));
  Register #(.width(32)) R26 (.D(in_2), .en(E26), .Q(Out26), .clk(Clock), .clr(Reset));
  Register #(.width(32)) R30 (.D(in_2), .en(E30), .Q(Out30), .clk(Clock), .clr(Reset));
  Register #(.width(32)) R03 (.D(in_2), .en(E03), .Q(Out03), .clk(Clock), .clr(Reset));
  Register #(.width(32)) R07 (.D(in_2), .en(E07), .Q(Out07), .clk(Clock), .clr(Reset));
  Register #(.width(32)) R11 (.D(in_2), .en(E11), .Q(Out11), .clk(Clock), .clr(Reset));
  Register #(.width(32)) R15 (.D(in_2), .en(E15), .Q(Out15), .clk(Clock), .clr(Reset));
  Register #(.width(32)) R19 (.D(in_2), .en(E19), .Q(Out19), .clk(Clock), .clr(Reset));
  Register #(.width(32)) R23 (.D(in_2), .en(E23), .Q(Out23), .clk(Clock), .clr(Reset));
  Register #(.width(32)) R27 (.D(in_2), .en(E27), .Q(Out27), .clk(Clock), .clr(Reset));
  Register #(.width(32)) R31 (.D(in_2), .en(E31), .Q(Out31), .clk(Clock), .clr(Reset));
  Multiplexer #(.select(5), .width(32), .enable("false")) multiplexer_1 (
    .in0(Out00), .in1(Out01), .in2(Out02), .in3(Out03), .in4(Out04), .in5(Out05), .in6(Out06), .in7(Ou07),
    .in8(Out08), .in9(Out09), .in10(Out10), .in11(Out11), .in12(Out12), .in13(Out13), .in14(Out14),
    .in15(Out15), .in16(Out16), .in17(Out17), .in18(Out18), .in19(Out19), .in20(Out20), .in21(Out21),
    .in22(Out22), .in23(Out23), .in24(Out24), .in25(Out25), .in26(Out26), .in27(Out27), .in28(Out28),
    .in29(Out29), .in30(Out30), .in31(Out31), .out(Output), .sel(Selector_A));
  Multiplexer #(.select(5), .width(32), .enable("false")) multiplexer_2 (
    .in0(Out00), .in1(Out01), .in2(Out02), .in3(Out03), .in4(Out04), .in5(Out05), .in6(Out06), .in7(Ou07),
    .in8(Out08), .in9(Out09), .in10(Out10), .in11(Out11), .in12(Out12), .in13(Out13), .in14(Out14),
    .in15(Out15), .in16(Out16), .in17(Out17), .in18(Out18), .in19(Out19), .in20(Out20), .in21(Out21),
    .in22(Out22), .in23(Out23), .in24(Out24), .in25(Out25), .in26(Out26), .in27(Out27), .in28(Out28),
    .in29(Out29), .in30(Out30), .in31(Out31), .out(Output_2), .sel(Selector_B));

  // Other names for the same wires on the sheet: Clk = Clock; DataAddress[4:0] = Data_Address; DataIn[31:0] = in_2;
  //   R_W = Read_Write; Rst = Reset; SelectA[4:0] = Selector_A; SelectB[4:0] = Selector_B

  // Notes on the sheet:
  //   Inputs
  //   Data In
  //   Outputs
  //   Data A
  //   Data B
endmodule

module ALU (
  input  [31:0] Data_A,
  input  [31:0] Data_B,
  input  [3:0] Selector,
  output [31:0] ALU_Output,
  output Zero_Flag,
  output Negative_Flag
);

  wire [31:0] Add, And, Div, Mul, Nor, Or, Sub, undriven, undriven_2, undriven_3, undriven_4, undriven_5,
       undriven_6, undriven_7, undriven_8, Xor;

  Adder #(.width(32)) adder_1 (.a(Data_A), .b(Data_B), .out(Add));  // open: cin, cout
  Subtractor #(.width(32)) subtractor_1 (.a(Data_A), .b(Data_B), .out(Sub));  // open: bin, bout
  Multiplier #(.width(32)) multiplier_1 (.a(Data_A), .b(Data_B), .out(Mul));  // open: cin, cout
  Divider #(.width(32)) divider_1 (.a(Data_A), .b(Data_B), .out(Div));  // open: upper, rem
  Multiplexer #(.select(4), .width(32), .enable("false")) multiplexer_1 (
    .in0(Add), .in1(Sub), .in2(Mul), .in3(Div), .in4(And), .in5(Or), .in6(Nor), .in7(Xor), .in8(undriven),
    .in9(undriven_2), .in10(undriven_3), .in11(undriven_4), .in12(undriven_5), .in13(undriven_6),
    .in14(undriven_7), .in15(undriven_8), .out(ALU_Output), .sel(Selector));
  assign And = Data_A & Data_B;  // AND_Gate and_1, 32 bits wide
  assign Or = Data_A | Data_B;  // OR_Gate or_1, 32 bits wide
  assign Nor = ~(Data_A | Data_B);  // NOR_Gate nor_1, 32 bits wide
  assign Xor = Data_A ^ Data_B;  // XOR_Gate xor_1, 32 bits wide
  Comparator #(.width(32)) comparator_1 (
    .a(ALU_Output), .b({32{1'b0}}), .eq(Zero_Flag), .lt(Negative_Flag));  // open: gt

  // Other names for the same wires on the sheet: A[31:0] = Data_A; B[31:0] = Data_B; Output[31:0] = ALU_Output

  // Notes on the sheet:
  //   INPUTS
  //   ARITHMETIC
  //   LOGIC
  //   OUTPUTS
endmodule
